// Logisim project project.circ as structural Verilog
module main (
  input  [7:0] INPUT
);

  wire ac_controler_1_clr, ac_controler_1_inc, alu_controller_1_e_out, and_1_out, ar_controler_1_clr,
       ar_controler_1_inc, ar_controler_1_ld, clock_1_out, Clr_T_count, controller_inc, controller_ld, E,
       e_controler_1_clear, e_controler_1_comp, e_controler_1_load, FGI, fgi_fgo_ien_controler_1_fgi_j,
       fgi_fgo_ien_controler_1_fgi_k, fgi_fgo_ien_controler_1_fgo_j, fgi_fgo_ien_controler_1_fgo_k,
       fgi_fgo_ien_controler_1_ien_j, fgi_fgo_ien_controler_1_ien_k, FGO, HLT, I, IEN, ir_controler_1_ld,
       j_k_ff_1_q, memory_controller_load, not_1_out, outp_controller_1_ld, pc_controler_1_clr,
       pc_controler_1_inc, pc_controler_1_ld, R, T_clear_counter_t_count_clear, tr_controle_1_ld;
  wire [2:0] S, T_count;
  wire [3:0] outr_1_hex_0, outr_1_hex_1;
  wire [15:0] AC, ALU, AR_out_6, controlled_buffer_1_out, controlled_buffer_2_out, DR, IR, multiplexer_1_out,
       PC_out_7, TR_out_6;

  // Probe on multiplexer_1_out[15]
  // Probe on multiplexer_1_out[13]
  // Probe on multiplexer_1_out[14]
  // Probe on multiplexer_1_out[12]
  // Probe on multiplexer_1_out[11]
  Multiplexer #(.select(3), .width(16)) multiplexer_1 (
    .in1(AR_out_6), .in2(PC_out_7), .in3(DR), .in4(AC), .in5(IR), .in6(TR_out_6),
    .in7(controlled_buffer_2_out), .out(multiplexer_1_out), .sel(S));  // open: in0, en
  // Probe on multiplexer_1_out[9]
  // Probe on multiplexer_1_out[10]
  // Probe on multiplexer_1_out[6]
  // Probe on multiplexer_1_out[8]
  // Probe on multiplexer_1_out[7]
  // Probe on multiplexer_1_out[5]
  // Probe on multiplexer_1_out[4]
  // Probe on multiplexer_1_out[3]
  // Probe on multiplexer_1_out[2]
  // Probe on multiplexer_1_out[1]
  // Probe on multiplexer_1_out[0]
  Clock clock_1 (.out(clock_1_out));
  J_K_Flip_Flop j_k_ff_1 (.J(1'b0), .clk(clock_1_out), .K(HLT), .Q(j_k_ff_1_q));  // open: Qn, preset, en, reset
  bus_controler bus_controller (.T({1'b0, T_count}), .R(R), .Bus_Select(S), .IR(IR));
  and and_1 (and_1_out, j_k_ff_1_q, clock_1_out);
  and and_2 (Clr_T_count, T_clear_counter_t_count_clear, HLT);
  T_clear_controler T_clear_counter (
    .T({1'b0, T_count}), .R(R), .IR(IR), .T_count_clear(T_clear_counter_t_count_clear));
  assign controlled_buffer_1_out = not_1_out ? multiplexer_1_out : 16'bz;  // Controlled_Buffer controlled_buffer_1
  RAM #(.addrWidth(12), .dataWidth(16)) ram_1 (
    .addr(AR_out_6[11:0]), .data(controlled_buffer_1_out), .clk(and_1_out), .ld(memory_controller_load));  // open: sel, clr
  assign controlled_buffer_2_out = memory_controller_load ? controlled_buffer_1_out : 16'bz;  // Controlled_Buffer controlled_buffer_2
  Memory_controler memory_controller (.T({1'b0, T_count}), .R(R), .IR(IR), .Load(memory_controller_load));
  DR_controler controller (.T({1'b0, T_count}), .IR(IR), .LD(controller_ld), .Inc(controller_inc));
  not not_1 (not_1_out, memory_controller_load);
  DR u_DR (
    .in_1(multiplexer_1_out), .inc(controller_inc), .load(controller_ld), .clock(and_1_out), .out_6(DR));  // open: clear
  TR_controle tr_controle_1 (.T({1'b0, T_count}), .LD(tr_controle_1_ld), .R(R));
  ALU_controller alu_controller_1 (
    .T({1'b0, T_count}), .AC(AC), .DR(DR), .INPR(INPUT), .E_In(E), .IR(IR), .OUT(ALU),
    .E_Out(alu_controller_1_e_out));
  TR TR (.in_1(multiplexer_1_out), .clock(and_1_out), .inc(tr_controle_1_ld), .out_6(TR_out_6));  // open: load, clear
  LED u_E (.in(E));
  E e_2 (
    .E_IN(alu_controller_1_e_out), .Comp(e_controler_1_comp), .Clock(e_controler_1_clear),
    .load(e_controler_1_load), .Clear(and_1_out), .E_OUT(E));
  E_controler e_controler_1 (
    .T({1'b0, T_count}), .IR(IR), .Comp(e_controler_1_comp), .Clear(e_controler_1_clear),
    .Load(e_controler_1_load));
  IR_controler ir_controler_1 (.T({1'b0, T_count}), .LD(ir_controler_1_ld), .R(R));
  LED u_I (.in(I));
  FGI_FGO_IEN_controler fgi_fgo_ien_controler_1 (
    .T({1'b0, T_count}), .R(R), .INPR(INPUT), .FGO_J(fgi_fgo_ien_controler_1_fgo_j),
    .FGO_K(fgi_fgo_ien_controler_1_fgo_k), .FGI_K(fgi_fgo_ien_controler_1_fgi_k), .IR(IR),
    .IEN_J(fgi_fgo_ien_controler_1_ien_j), .IEN_K(fgi_fgo_ien_controler_1_ien_k),
    .FGI_J(fgi_fgo_ien_controler_1_fgi_j));
  IR u_IR (.Bus_IN(multiplexer_1_out), .Load(ir_controler_1_ld), .Clock(and_1_out), .Bus_OUT(IR), .S(HLT), .I(I));
  LED I_EN (.in(IEN));
  LED u_FGI (.in(FGI));
  I_EN u_IEN (
    .EIN_J(fgi_fgo_ien_controler_1_ien_j), .Clock(and_1_out), .EIN_K(fgi_fgo_ien_controler_1_ien_k),
    .EIN_OUT(IEN));
  FGI FGI_2 (
    .FGI_J(fgi_fgo_ien_controler_1_fgi_j), .Clock(and_1_out), .FGI_K(fgi_fgo_ien_controler_1_fgi_k),
    .FGI_OUT(FGI));
  LED u_FGO (.in(FGO));
  FGO FGO_2 (
    .FGO_J(fgi_fgo_ien_controler_1_fgo_j), .Clock(and_1_out), .FGO_K(fgi_fgo_ien_controler_1_fgo_k),
    .FGO_OUT(FGO));
  PC PC (
    .increas(pc_controler_1_inc), .load(pc_controler_1_ld), .clock(and_1_out), .clear(pc_controler_1_clr),
    .in_5(multiplexer_1_out), .out_7(PC_out_7));  // open: out_6
  PC_controler pc_controler_1 (
    .T({1'b0, T_count}), .R(R), .DR(DR), .AC(AC), .IR(IR), .LD(pc_controler_1_ld), .Inc(pc_controler_1_inc),
    .Clr(pc_controler_1_clr), .FGI(FGI), .FGO(FGO));  // open: E
  OUTP_controller outp_controller_1 (.T({1'b0, T_count}), .IR(IR), .LD(outp_controller_1_ld));
  OUTR outr_1 (
    .BUS_IN(multiplexer_1_out), .L_OUT(outp_controller_1_ld), .Clock(and_1_out), .Hex_0(outr_1_hex_0),
    .Hex_1(outr_1_hex_1));
  AR AR (
    .in_1(multiplexer_1_out), .clock(and_1_out), .inc(ar_controler_1_inc), .clear(ar_controler_1_clr),
    .load(ar_controler_1_ld), .out_6(AR_out_6));
  AR_controler ar_controler_1 (
    .T({1'b0, T_count}), .R(R), .IR(IR), .LD(ar_controler_1_ld), .Clr(ar_controler_1_clr),
    .Inc(ar_controler_1_inc));
  Hex_Digit_Display hex_digit_display_1 (.value(outr_1_hex_0));  // open: dp
  Hex_Digit_Display hex_digit_display_2 (.value(outr_1_hex_1));  // open: dp
  LED u_R (.in(R));
  Hex_Digit_Display hex_digit_display_3 (.value({1'b0, T_count}));  // open: dp
  R r_2 (.T_count(T_count), .E_IN(IEN), .FGI(FGI), .FGO(FGO), .E_OUT(R));
  AC_controler ac_controler_1 (.T({1'b0, T_count}), .IR(IR), .Clr(ac_controler_1_clr), .Inc(ac_controler_1_inc));
  AC u_AC (.in_1(ALU), .increas(ac_controler_1_inc), .clock(and_1_out), .CLear(ac_controler_1_clr), .out_5(AC));
  T_count u_T_count (.Clock(and_1_out), .Clear(Clr_T_count), .OUT(T_count));

  // Other names for the same wires on the sheet: INP[7:0] = INPUT

  // Notes on the sheet:
  //   BUS  15   14   13   12   11   10    9    8    7    6    5    4    3    2    1   0
  //   BUS LOAD
  //   OUTP
endmodule

module PC (
  input  increas,
  input  load,
  input  clock,
  input  clear,
  input  [15:0] in_5,
  output out_6,
  output [15:0] out_7
);

  wire or_1_out;
  wire [11:0] adder_12_1_coutput, multiplexer_1_out;

  Multiplexer #(.width(12)) multiplexer_1 (
    .in0(in_5[11:0]), .in1(adder_12_1_coutput), .out(multiplexer_1_out), .sel(increas));  // open: en
  or or_1 (or_1_out, increas, load);
  adder_12 adder_12_1 (.X(12'h1), .Y(out_7[11:0]), .coutput(adder_12_1_coutput), .cout(out_6), .cin(1'b0));
  Register #(.width(12)) register_1 (.D(multiplexer_1_out), .en(or_1_out), .Q(out_7[11:0]), .clk(clock), .clr(clear));

  assign out_7[15:12] = 4'b0000;
endmodule

module AC (
  input  [15:0] in_1,
  input  increas,
  input  clock,
  input  CLear,
  output [15:0] out_5
);

  wire [15:0] adder_16_1_output, multiplexer_1_out;

  adder_16 adder_16_1 (.cin(1'b0), .X(16'h1), .Y(out_5), .\output (adder_16_1_output));  // open: cout
  Multiplexer #(.width(16)) multiplexer_1 (
    .in0(in_1), .in1(adder_16_1_output), .out(multiplexer_1_out), .sel(increas));  // open: en
  Register #(.width(16), .trigger("falling")) register_1 (
    .D(multiplexer_1_out), .Q(out_5), .clk(clock), .clr(CLear));  // open: en
endmodule

module TR (
  input  [15:0] in_1,
  input  load,
  input  clock,
  input  inc,
  input  clear,
  output [15:0] out_6
);

  wire or_1_out;
  wire [15:0] adder_16_1_output, multiplexer_1_out;

  or or_1 (or_1_out, load, inc);
  adder_16 adder_16_1 (.cin(1'b0), .X(16'h1), .Y(out_6), .\output (adder_16_1_output));  // open: cout
  Multiplexer #(.width(16)) multiplexer_1 (
    .in0(in_1), .in1(adder_16_1_output), .out(multiplexer_1_out), .sel(inc));  // open: en
  Register #(.width(16)) register_1 (.en(or_1_out), .Q(out_6), .clk(clock), .clr(clear));  // open: D
endmodule

module AR (
  input  [15:0] in_1,
  input  clock,
  input  inc,
  input  clear,
  input  load,
  output [15:0] out_6
);

  wire or_1_out;
  wire [11:0] adder_12_1_coutput, multiplexer_1_out;

  Multiplexer #(.width(12)) multiplexer_1 (
    .in0(in_1[11:0]), .in1(adder_12_1_coutput), .out(multiplexer_1_out), .sel(inc));  // open: en
  or or_1 (or_1_out, inc, load);
  adder_12 adder_12_1 (.X(12'h1), .Y(out_6[11:0]), .coutput(adder_12_1_coutput), .cin(1'b0));  // open: cout
  Register #(.width(12)) register_1 (.D(multiplexer_1_out), .en(or_1_out), .Q(out_6[11:0]), .clk(clock), .clr(clear));

  assign out_6[15:12] = 4'b0000;
endmodule

module DR (
  input  [15:0] in_1,
  input  inc,
  input  load,
  input  clock,
  input  clear,
  output [15:0] out_6
);

  wire or_1_out;
  wire [15:0] adder_16_1_output, multiplexer_1_out;

  Multiplexer #(.width(16)) multiplexer_1 (
    .in0(in_1), .in1(adder_16_1_output), .out(multiplexer_1_out), .sel(inc));  // open: en
  or or_1 (or_1_out, inc, load);
  Register #(.width(16)) register_1 (.D(multiplexer_1_out), .en(or_1_out), .Q(out_6), .clk(clock), .clr(clear));
  adder_16 adder_16_1 (.cin(1'b0), .X(16'h1), .Y(out_6), .\output (adder_16_1_output));  // open: cout
endmodule

module IR (
  input  [15:0] Bus_IN,
  input  Load,
  input  Clock,
  output [15:0] Bus_OUT,
  output S,
  output I
);

  Register #(.width(16)) register_1 (.D(Bus_IN), .en(Load), .Q(Bus_OUT), .clk(Clock));  // open: clr
  and and_1 (S, Bus_OUT[0], ~Bus_OUT[1], ~Bus_OUT[2], ~Bus_OUT[3], ~Bus_OUT[4], ~Bus_OUT[5], ~Bus_OUT[6], ~Bus_OUT[7], ~Bus_OUT[8], ~Bus_OUT[9], ~Bus_OUT[10], ~Bus_OUT[11], Bus_OUT[12], Bus_OUT[13], Bus_OUT[14], ~Bus_OUT[15]);  // AND_Gate

  assign I = Bus_OUT[15];
endmodule

module E (
  input  E_IN,
  input  Comp,
  input  load,
  input  Clock,
  input  Clear,
  output E_OUT
);

  wire and_1_out, multiplexer_1_out;

  Multiplexer multiplexer_1 (.in0(E_IN), .in1(Comp), .out(multiplexer_1_out), .sel(Comp));  // open: en
  and and_1 (and_1_out, multiplexer_1_out, Comp);
  J_K_Flip_Flop j_k_ff_1 (
    .J(multiplexer_1_out), .clk(Clock), .K(and_1_out), .Q(E_OUT), .en(load), .reset(Clear));  // open: Qn, preset
endmodule

module OUTR (
  input  [15:0] BUS_IN,
  input  L_OUT,
  input  Clock,
  output [3:0] Hex_0,
  output [3:0] Hex_1
);

  wire [15:8] register_1_q;

  Register #(.width(16)) register_1 (
    .D({{8{1'b0}}, BUS_IN[7:0]}), .en(L_OUT), .Q({register_1_q, Hex_1, Hex_0}), .clk(Clock));  // open: clr
endmodule

module FGI (
  input  FGI_J,
  input  Clock,
  input  FGI_K,
  output FGI_OUT
);

  J_K_Flip_Flop j_k_ff_1 (.J(FGI_J), .clk(Clock), .K(FGI_K), .Q(FGI_OUT));  // open: Qn, preset, en, reset
endmodule

module FGO (
  input  FGO_J,
  input  Clock,
  input  FGO_K,
  output FGO_OUT
);

  J_K_Flip_Flop j_k_ff_1 (.J(FGO_J), .clk(Clock), .K(FGO_K), .Q(FGO_OUT));  // open: Qn, preset, en, reset
endmodule

module T_count (
  input  Clock,
  input  Clear,
  output [2:0] OUT
);

  wire and_1_out, or_1_out;
  wire [2:0] adder_3_1_out_4;

  and and_1 (and_1_out, OUT[2], OUT[1], OUT[0]);
  adder_3 adder_3_1 (.cin(1'b0), .X(OUT), .Y(3'b001), .out_4(adder_3_1_out_4));  // open: out_5
  or or_1 (or_1_out, Clear, and_1_out);
  Register #(.width(3)) register_1 (.D(adder_3_1_out_4), .Q(OUT), .clk(Clock), .clr(or_1_out));  // open: en
endmodule

module bus_controler (
  input  [15:0] IR,
  input  [3:0] T,
  input  R,
  output [2:0] Bus_Select
);

  wire and_2_out, and_3_out, and_4_out, and_5_out, and_6_out, and_7_out, and_8_out, and_9_out, and_10_out,
       and_11_out, and_12_out, and_13_out, and_14_out, decoder_1_out0, decoder_1_out1, decoder_1_out2,
       decoder_1_out3, decoder_1_out4, decoder_1_out5, decoder_1_out6, decoder_1_out7, decoder_2_out0,
       decoder_2_out1, decoder_2_out2, decoder_2_out3, decoder_2_out4, decoder_2_out5, decoder_2_out6,
       decoder_2_out7, or_1_out, or_2_out, or_3_out, or_4_out, or_5_out, or_6_out, p;
  wire [2:0] priority_encoder_1_out;

  Decoder #(.select(3)) decoder_1 (
    .out0(decoder_1_out0), .out1(decoder_1_out1), .out2(decoder_1_out2), .out3(decoder_1_out3),
    .out4(decoder_1_out4), .out5(decoder_1_out5), .out6(decoder_1_out6), .out7(decoder_1_out7), .sel(T[2:0]));  // open: en
  Decoder #(.select(3)) decoder_2 (
    .out0(decoder_2_out0), .out1(decoder_2_out1), .out2(decoder_2_out2), .out3(decoder_2_out3),
    .out4(decoder_2_out4), .out5(decoder_2_out5), .out6(decoder_2_out6), .out7(decoder_2_out7),
    .sel(IR[14:12]));  // open: en
  and and_1 (p, decoder_2_out7, IR[15], decoder_1_out3);
  and and_2 (and_2_out, decoder_2_out5, decoder_1_out4);
  and and_3 (and_3_out, decoder_1_out4, decoder_2_out4);
  and and_4 (and_4_out, decoder_2_out5, decoder_1_out5);
  and and_5 (and_5_out, decoder_2_out6, decoder_1_out6);
  and and_6 (and_6_out, decoder_2_out2, decoder_1_out5);
  and and_7 (and_7_out, decoder_2_out3, decoder_1_out4);
  and and_8 (and_8_out, IR[10], p);
  and and_9 (and_9_out, decoder_1_out2, ~R);  // AND_Gate
  and and_10 (and_10_out, decoder_1_out1, R);
  or or_1 (or_1_out, decoder_1_out0, and_2_out);
  or or_2 (or_2_out, and_3_out, and_4_out);
  or or_3 (or_3_out, and_5_out, and_6_out);
  or or_4 (or_4_out, and_7_out, and_8_out);
  and and_11 (and_11_out, decoder_1_out1, ~R);  // AND_Gate
  and and_12 (and_12_out, ~decoder_2_out7, IR[15], decoder_1_out3);  // AND_Gate
  or or_5 (or_5_out, decoder_2_out0, decoder_2_out1, decoder_2_out2, decoder_2_out6);
  and and_13 (and_13_out, or_5_out, decoder_1_out4);
  and and_14 (and_14_out, ~or_2_out, ~and_9_out, ~or_3_out, ~or_1_out, ~or_4_out, ~and_10_out, ~or_6_out);  // AND_Gate
  or or_6 (or_6_out, and_11_out, and_12_out, and_13_out);
  Priority_Encoder priority_encoder_1 (
    .in0(and_14_out), .in1(or_2_out), .in2(or_1_out), .in3(or_3_out), .in4(or_4_out), .in5(and_9_out),
    .in6(and_10_out), .in7(or_6_out), .out(priority_encoder_1_out));  // open: en_in, gs, en_out
  Multiplexer #(.select(3), .width(3)) multiplexer_1 (
    .in0(3'b000), .in1(3'b001), .in2(3'b010), .in3(3'b011), .in4(3'b100), .in5(3'b101), .in6(3'b110),
    .in7(3'b111), .out(Bus_Select), .sel(priority_encoder_1_out));  // open: en
endmodule

module T_clear_controler (
  input  [15:0] IR,
  input  [3:0] T,
  input  R,
  output T_count_clear
);

  wire and_1_out, and_2_out, and_3_out, and_4_out, and_5_out, and_6_out, and_7_out, decoder_1_out0,
       decoder_1_out1, decoder_1_out2, decoder_1_out3, decoder_1_out4, decoder_1_out5, decoder_1_out6,
       decoder_1_out7, decoder_2_out0, decoder_2_out1, decoder_2_out2, decoder_2_out3, decoder_2_out4,
       decoder_2_out5, decoder_2_out6, decoder_2_out7, or_1_out;

  Decoder #(.select(3)) decoder_1 (
    .out0(decoder_1_out0), .out1(decoder_1_out1), .out2(decoder_1_out2), .out3(decoder_1_out3),
    .out4(decoder_1_out4), .out5(decoder_1_out5), .out6(decoder_1_out6), .out7(decoder_1_out7), .sel(T[2:0]));  // open: en
  Decoder #(.select(3)) decoder_2 (
    .out0(decoder_2_out0), .out1(decoder_2_out1), .out2(decoder_2_out2), .out3(decoder_2_out3),
    .out4(decoder_2_out4), .out5(decoder_2_out5), .out6(decoder_2_out6), .out7(decoder_2_out7),
    .sel(IR[14:12]));  // open: en
  or or_1 (or_1_out, decoder_2_out0, decoder_2_out1, decoder_2_out2, decoder_2_out5);
  and and_1 (and_1_out, decoder_1_out5, decoder_2_out3);
  and and_2 (and_2_out, decoder_2_out7, ~IR[15], decoder_1_out4);  // AND_Gate
  and and_3 (and_3_out, decoder_1_out4, IR[15], decoder_2_out7);
  and and_4 (and_4_out, decoder_1_out3, R);
  and and_5 (and_5_out, decoder_2_out4, decoder_1_out5);
  and and_6 (and_6_out, decoder_2_out6, decoder_1_out7);
  and and_7 (and_7_out, or_1_out, decoder_1_out6);
  or or_2 (T_count_clear, and_7_out, and_2_out, and_3_out, and_1_out, and_5_out, and_6_out, and_4_out);
endmodule

module AR_controler (
  input  [15:0] IR,
  input  [3:0] T,
  input  R,
  output LD,
  output Clr,
  output Inc
);

  wire and_1_out, and_2_out, and_3_out, decoder_1_out0, decoder_1_out1, decoder_1_out2, decoder_1_out3,
       decoder_1_out4, decoder_1_out5, decoder_1_out6, decoder_1_out7, decoder_2_out0, decoder_2_out1,
       decoder_2_out2, decoder_2_out3, decoder_2_out4, decoder_2_out5, decoder_2_out6, decoder_2_out7;

  Decoder #(.select(3)) decoder_1 (
    .out0(decoder_1_out0), .out1(decoder_1_out1), .out2(decoder_1_out2), .out3(decoder_1_out3),
    .out4(decoder_1_out4), .out5(decoder_1_out5), .out6(decoder_1_out6), .out7(decoder_1_out7), .sel(T[2:0]));  // open: en
  Decoder #(.select(3)) decoder_2 (
    .out0(decoder_2_out0), .out1(decoder_2_out1), .out2(decoder_2_out2), .out3(decoder_2_out3),
    .out4(decoder_2_out4), .out5(decoder_2_out5), .out6(decoder_2_out6), .out7(decoder_2_out7),
    .sel(IR[14:12]));  // open: en
  and and_1 (and_1_out, ~R, decoder_1_out0);  // AND_Gate
  and and_2 (and_2_out, ~decoder_2_out7, IR[15], decoder_1_out3);  // AND_Gate
  and and_3 (and_3_out, ~R, decoder_1_out2);  // AND_Gate
  and and_4 (Clr, R, decoder_1_out0);
  and and_5 (Inc, decoder_2_out5, decoder_1_out4);
  or or_1 (LD, and_1_out, and_2_out, and_3_out);
endmodule

module IR_controler (
  input  R,
  input  [3:0] T,
  output LD
);

  wire decoder_1_out0, decoder_1_out1, decoder_1_out2, decoder_1_out3, decoder_1_out4, decoder_1_out5,
       decoder_1_out6, decoder_1_out7;

  Decoder #(.select(3)) decoder_1 (
    .out0(decoder_1_out0), .out1(decoder_1_out1), .out2(decoder_1_out2), .out3(decoder_1_out3),
    .out4(decoder_1_out4), .out5(decoder_1_out5), .out6(decoder_1_out6), .out7(decoder_1_out7), .sel(T[2:0]));  // open: en
  and and_1 (LD, ~R, decoder_1_out1);  // AND_Gate
endmodule

module TR_controle (
  input  R,
  input  [3:0] T,
  output LD
);

  wire decoder_1_out0, decoder_1_out1, decoder_1_out2, decoder_1_out3, decoder_1_out4, decoder_1_out5,
       decoder_1_out6, decoder_1_out7;

  Decoder #(.select(3)) decoder_1 (
    .out0(decoder_1_out0), .out1(decoder_1_out1), .out2(decoder_1_out2), .out3(decoder_1_out3),
    .out4(decoder_1_out4), .out5(decoder_1_out5), .out6(decoder_1_out6), .out7(decoder_1_out7), .sel(T[2:0]));  // open: en
  and and_1 (LD, ~R, decoder_1_out0);  // AND_Gate
endmodule

module DR_controler (
  input  [15:0] IR,
  input  [3:0] T,
  output LD,
  output Inc
);

  wire decoder_1_out0, decoder_1_out1, decoder_1_out2, decoder_1_out3, decoder_1_out4, decoder_1_out5,
       decoder_1_out6, decoder_1_out7, decoder_2_out0, decoder_2_out1, decoder_2_out2, decoder_2_out3,
       decoder_2_out4, decoder_2_out5, decoder_2_out6, decoder_2_out7, or_1_out;

  Decoder #(.select(3)) decoder_1 (
    .out0(decoder_1_out0), .out1(decoder_1_out1), .out2(decoder_1_out2), .out3(decoder_1_out3),
    .out4(decoder_1_out4), .out5(decoder_1_out5), .out6(decoder_1_out6), .out7(decoder_1_out7), .sel(T[2:0]));  // open: en
  Decoder #(.select(3)) decoder_2 (
    .out0(decoder_2_out0), .out1(decoder_2_out1), .out2(decoder_2_out2), .out3(decoder_2_out3),
    .out4(decoder_2_out4), .out5(decoder_2_out5), .out6(decoder_2_out6), .out7(decoder_2_out7),
    .sel(IR[14:12]));  // open: en
  or or_1 (or_1_out, decoder_2_out0, decoder_2_out1, decoder_2_out2, decoder_2_out6);
  and and_1 (Inc, decoder_2_out6, decoder_1_out5);
  and and_2 (LD, decoder_1_out4, or_1_out);
endmodule

module PC_controler (
  input  [15:0] IR,
  input  [3:0] T,
  input  R,
  input  FGI,
  input  FGO,
  input  E,
  input  [15:0] DR,
  input  [15:0] AC,
  output LD,
  output Inc,
  output Clr
);

  wire and_3_out, and_4_out, and_5_out, and_6_out, and_7_out, and_8_out, and_9_out, and_10_out, and_11_out,
       and_12_out, and_13_out, decoder_1_out0, decoder_1_out1, decoder_1_out2, decoder_1_out3,
       decoder_1_out4, decoder_1_out5, decoder_1_out6, decoder_1_out7, decoder_2_out0, decoder_2_out1,
       decoder_2_out2, decoder_2_out3, decoder_2_out4, decoder_2_out5, decoder_2_out6, decoder_2_out7,
       not_1_out, not_2_out, or_1_out, or_2_out, p, r_t;

  Decoder #(.select(3)) decoder_1 (
    .out0(decoder_1_out0), .out1(decoder_1_out1), .out2(decoder_1_out2), .out3(decoder_1_out3),
    .out4(decoder_1_out4), .out5(decoder_1_out5), .out6(decoder_1_out6), .out7(decoder_1_out7), .sel(T[2:0]));  // open: en
  not not_1 (not_1_out, or_1_out);
  or or_1 (or_1_out, DR[0], DR[1], DR[2], DR[3], DR[4], DR[5], DR[6], DR[7], DR[8], DR[10], DR[11], DR[12], DR[13], DR[9], DR[14], DR[15]);
  or or_2 (or_2_out, AC[0], AC[1], AC[2], AC[3], AC[4], AC[5], AC[6], AC[7], AC[8], AC[10], AC[11], AC[12], AC[13], AC[9], AC[14], AC[15]);
  not not_2 (not_2_out, or_2_out);
  Decoder #(.select(3)) decoder_2 (
    .out0(decoder_2_out0), .out1(decoder_2_out1), .out2(decoder_2_out2), .out3(decoder_2_out3),
    .out4(decoder_2_out4), .out5(decoder_2_out5), .out6(decoder_2_out6), .out7(decoder_2_out7),
    .sel(IR[14:12]));  // open: en
  and and_1 (p, decoder_2_out7, IR[15], decoder_1_out3);
  and and_2 (r_t, decoder_2_out7, ~IR[15], decoder_1_out3);  // AND_Gate
  and and_3 (and_3_out, decoder_2_out4, decoder_1_out4);
  and and_4 (and_4_out, decoder_2_out5, decoder_1_out5);
  and and_5 (and_5_out, ~R, decoder_1_out1);  // AND_Gate
  and and_6 (and_6_out, R, decoder_1_out2);
  and and_7 (and_7_out, not_1_out, decoder_2_out6, decoder_1_out6);
  and and_8 (and_8_out, ~AC[15], IR[4], r_t);  // AND_Gate
  and and_9 (and_9_out, AC[15], IR[3], r_t);
  and and_10 (and_10_out, not_2_out, IR[2], r_t);
  and and_11 (and_11_out, ~E, IR[1], r_t);  // AND_Gate
  and and_12 (and_12_out, IR[10], FGI, p);
  and and_13 (and_13_out, IR[9], FGO, p);
  and and_14 (Clr, R, decoder_1_out1);
  or or_3 (LD, and_3_out, and_4_out);
  or or_4 (Inc, and_6_out, and_8_out, and_9_out, and_5_out, and_7_out, and_10_out, and_11_out, and_12_out, and_13_out);
endmodule

module AC_controler (
  input  [15:0] IR,
  input  [3:0] T,
  output Clr,
  output Inc
);

  wire decoder_1_out0, decoder_1_out1, decoder_1_out2, decoder_1_out3, decoder_1_out4, decoder_1_out5,
       decoder_1_out6, decoder_1_out7, decoder_2_out0, decoder_2_out1, decoder_2_out2, decoder_2_out3,
       decoder_2_out4, decoder_2_out5, decoder_2_out6, decoder_2_out7, p, r;

  Decoder #(.select(3)) decoder_1 (
    .out0(decoder_1_out0), .out1(decoder_1_out1), .out2(decoder_1_out2), .out3(decoder_1_out3),
    .out4(decoder_1_out4), .out5(decoder_1_out5), .out6(decoder_1_out6), .out7(decoder_1_out7), .sel(T[2:0]));  // open: en
  Decoder #(.select(3)) decoder_2 (
    .out0(decoder_2_out0), .out1(decoder_2_out1), .out2(decoder_2_out2), .out3(decoder_2_out3),
    .out4(decoder_2_out4), .out5(decoder_2_out5), .out6(decoder_2_out6), .out7(decoder_2_out7),
    .sel(IR[14:12]));  // open: en
  and and_1 (Clr, IR[11], r);
  and and_2 (Inc, IR[5], r);
  and and_3 (r, decoder_1_out3, ~IR[15], decoder_2_out7);  // AND_Gate
  and and_4 (p, decoder_2_out7, IR[15], decoder_1_out3);
endmodule

module FGI_FGO_IEN_controler (
  input  [15:0] IR,
  input  [3:0] T,
  input  R,
  input  [7:0] INPR,
  output FGO_K,
  output FGI_K,
  output IEN_J,
  output IEN_K,
  output FGI_J,
  output FGO_J
);

  wire and_2_out, and_3_out, decoder_1_out1, decoder_1_out2, decoder_1_out3, decoder_1_out4, decoder_1_out5,
       decoder_1_out6, decoder_1_out7, decoder_2_out0, decoder_2_out1, decoder_2_out2, decoder_2_out3,
       decoder_2_out4, decoder_2_out5, decoder_2_out6, decoder_2_out7, p;

  or or_1 (FGI_J, INPR[7], INPR[6], INPR[5], INPR[4], INPR[3], INPR[2], INPR[1], INPR[0]);
  Decoder #(.select(3)) decoder_1 (
    .out0(FGO_J), .out1(decoder_1_out1), .out2(decoder_1_out2), .out3(decoder_1_out3), .out4(decoder_1_out4),
    .out5(decoder_1_out5), .out6(decoder_1_out6), .out7(decoder_1_out7), .sel(T[2:0]));  // open: en
  Decoder #(.select(3)) decoder_2 (
    .out0(decoder_2_out0), .out1(decoder_2_out1), .out2(decoder_2_out2), .out3(decoder_2_out3),
    .out4(decoder_2_out4), .out5(decoder_2_out5), .out6(decoder_2_out6), .out7(decoder_2_out7),
    .sel(IR[14:12]));  // open: en
  and and_1 (p, IR[15], decoder_1_out3, decoder_2_out7);
  and and_2 (and_2_out, R, decoder_1_out2);
  and and_3 (and_3_out, IR[6], p);
  and and_4 (FGO_K, p, IR[10]);
  and and_5 (FGI_K, IR[11], p);
  and and_6 (IEN_J, IR[7], p);
  or or_2 (IEN_K, and_2_out, and_3_out);
endmodule

module OUTP_controller (
  input  [15:0] IR,
  input  [3:0] T,
  output LD
);

  wire decoder_1_out0, decoder_1_out1, decoder_1_out2, decoder_1_out3, decoder_1_out4, decoder_1_out5,
       decoder_1_out6, decoder_1_out7, decoder_2_out0, decoder_2_out1, decoder_2_out2, decoder_2_out3,
       decoder_2_out4, decoder_2_out5, decoder_2_out6, decoder_2_out7, p;

  Decoder #(.select(3)) decoder_1 (
    .out0(decoder_1_out0), .out1(decoder_1_out1), .out2(decoder_1_out2), .out3(decoder_1_out3),
    .out4(decoder_1_out4), .out5(decoder_1_out5), .out6(decoder_1_out6), .out7(decoder_1_out7), .sel(T[2:0]));  // open: en
  Decoder #(.select(3)) decoder_2 (
    .out0(decoder_2_out0), .out1(decoder_2_out1), .out2(decoder_2_out2), .out3(decoder_2_out3),
    .out4(decoder_2_out4), .out5(decoder_2_out5), .out6(decoder_2_out6), .out7(decoder_2_out7),
    .sel(IR[14:12]));  // open: en
  and and_1 (p, decoder_1_out3, IR[15], decoder_2_out7);
  and and_2 (LD, IR[10], p);
endmodule

module E_controler (
  input  [15:0] IR,
  input  [3:0] T,
  output Comp,
  output Clear,
  output Load
);

  wire and_5_out, and_6_out, and_7_out, decoder_1_out0, decoder_1_out1, decoder_1_out2, decoder_1_out3,
       decoder_1_out4, decoder_1_out5, decoder_1_out6, decoder_1_out7, decoder_2_out0, decoder_2_out1,
       decoder_2_out2, decoder_2_out3, decoder_2_out4, decoder_2_out5, decoder_2_out6, decoder_2_out7, p, r;

  Decoder #(.select(3)) decoder_1 (
    .out0(decoder_1_out0), .out1(decoder_1_out1), .out2(decoder_1_out2), .out3(decoder_1_out3),
    .out4(decoder_1_out4), .out5(decoder_1_out5), .out6(decoder_1_out6), .out7(decoder_1_out7), .sel(T[2:0]));  // open: en
  Decoder #(.select(3)) decoder_2 (
    .out0(decoder_2_out0), .out1(decoder_2_out1), .out2(decoder_2_out2), .out3(decoder_2_out3),
    .out4(decoder_2_out4), .out5(decoder_2_out5), .out6(decoder_2_out6), .out7(decoder_2_out7),
    .sel(IR[14:12]));  // open: en
  and and_1 (p, decoder_1_out3, IR[15], decoder_2_out7);
  and and_2 (r, decoder_1_out3, ~IR[15], decoder_2_out7);  // AND_Gate
  and and_3 (Comp, IR[8], r);
  and and_4 (Clear, IR[10], r);
  and and_5 (and_5_out, IR[7], r);
  and and_6 (and_6_out, decoder_1_out5, decoder_2_out1);
  and and_7 (and_7_out, IR[6], r);
  or or_1 (Load, and_5_out, and_6_out, and_7_out);
endmodule

module ALU_controller (
  input  [15:0] IR,
  input  [3:0] T,
  input  [15:0] AC,
  input  [15:0] DR,
  input  [7:0] INPR,
  input  E_In,
  output [15:0] OUT,
  output E_Out
);

  wire adder_16_1_cout, and_4_out, and_5_out, and_6_out, and_7_out, and_8_out, and_9_out, and_10_out,
       and_11_out, and_12_out, and_13_out, decoder_1_out0, decoder_1_out1, decoder_1_out2, decoder_1_out3,
       decoder_1_out4, decoder_1_out5, decoder_1_out6, decoder_1_out7, decoder_2_out0, decoder_2_out1,
       decoder_2_out2, decoder_2_out3, decoder_2_out4, decoder_2_out5, decoder_2_out6, decoder_2_out7,
       not_2_out, or_1_out, p, r;
  wire [2:0] S;
  wire [15:0] adder_16_1_output, and_1_out, not_1_out, register_1_q, register_2_q, shifter_1_out,
       shifter_2_out;

  Shifter #(.width(16)) shifter_1 (.in(AC), .\dist (4'b0001), .out(shifter_1_out));
  Shifter #(.width(16), .shift("lr")) shifter_2 (.in(AC), .\dist (4'b0001), .out(shifter_2_out));
  Decoder #(.select(3)) decoder_1 (
    .out0(decoder_1_out0), .out1(decoder_1_out1), .out2(decoder_1_out2), .out3(decoder_1_out3),
    .out4(decoder_1_out4), .out5(decoder_1_out5), .out6(decoder_1_out6), .out7(decoder_1_out7), .sel(T[2:0]));  // open: en
  assign not_1_out = ~AC;  // NOT_Gate not_1, 16 bits wide
  Register #(.width(16), .trigger("high")) register_1 (
    .D({shifter_1_out[15:1], E_In}), .Q(register_1_q), .clk(1'b1));  // open: en, clr
  Register #(.width(16), .trigger("high")) register_2 (
    .D({E_In, shifter_2_out[14:0]}), .Q(register_2_q), .clk(1'b1));  // open: en, clr
  assign and_1_out = DR & AC;  // AND_Gate and_1, 16 bits wide
  Decoder #(.select(3)) decoder_2 (
    .out0(decoder_2_out0), .out1(decoder_2_out1), .out2(decoder_2_out2), .out3(decoder_2_out3),
    .out4(decoder_2_out4), .out5(decoder_2_out5), .out6(decoder_2_out6), .out7(decoder_2_out7),
    .sel(IR[14:12]));  // open: en
  adder_16 adder_16_1 (.cin(1'b0), .X(DR), .Y(AC), .\output (adder_16_1_output), .cout(adder_16_1_cout));
  and and_2 (p, decoder_1_out3, IR[15], decoder_2_out7);
  and and_3 (r, decoder_1_out3, ~IR[15], decoder_2_out7);  // AND_Gate
  Multiplexer #(.select(3), .width(16)) multiplexer_1 (
    .in0(AC), .in1(DR), .in2(not_1_out), .in3(register_1_q), .in4(register_2_q), .in5(and_1_out),
    .in6(adder_16_1_output), .in7({{8{1'b0}}, INPR}), .out(OUT), .sel(S));  // open: en
  and and_4 (and_4_out, ~S[2], S[1], S[0]);  // AND_Gate
  assign E_Out = and_6_out ? AC[0] : 1'bz;  // Controlled_Buffer controlled_buffer_1
  assign E_Out = and_4_out ? AC[15] : 1'bz;  // Controlled_Buffer controlled_buffer_2
  and and_5 (and_5_out, S[2], S[1], ~S[0]);  // AND_Gate
  and and_6 (and_6_out, S[2], ~S[1], ~S[0]);  // AND_Gate
  assign E_Out = and_5_out ? adder_16_1_cout : 1'bz;  // Controlled_Buffer controlled_buffer_3
  or or_1 (or_1_out, and_7_out, and_8_out, and_9_out, and_10_out, and_11_out, and_12_out, and_13_out);
  and and_7 (and_7_out, IR[9], r);
  and and_8 (and_8_out, decoder_2_out1, decoder_1_out5);
  and and_9 (and_9_out, decoder_2_out0, decoder_1_out5);
  and and_10 (and_10_out, IR[6], r);
  and and_11 (and_11_out, IR[11], p);
  and and_12 (and_12_out, IR[7], r);
  and and_13 (and_13_out, decoder_2_out2, decoder_1_out5);
  not not_2 (not_2_out, or_1_out);
  Priority_Encoder priority_encoder_1 (
    .in0(not_2_out), .in1(and_13_out), .in2(and_7_out), .in3(and_10_out), .in4(and_12_out), .in5(and_9_out),
    .in6(and_8_out), .in7(and_11_out), .out(S));  // open: en_in, gs, en_out
endmodule

module Memory_controler (
  input  [15:0] IR,
  input  [3:0] T,
  input  R,
  output Load
);

  wire and_1_out, and_2_out, and_3_out, and_4_out, decoder_1_out0, decoder_1_out1, decoder_1_out2,
       decoder_1_out3, decoder_1_out4, decoder_1_out5, decoder_1_out6, decoder_1_out7, decoder_2_out0,
       decoder_2_out1, decoder_2_out2, decoder_2_out3, decoder_2_out4, decoder_2_out5, decoder_2_out6,
       decoder_2_out7, or_1_out;

  Decoder #(.select(3)) decoder_1 (
    .out0(decoder_1_out0), .out1(decoder_1_out1), .out2(decoder_1_out2), .out3(decoder_1_out3),
    .out4(decoder_1_out4), .out5(decoder_1_out5), .out6(decoder_1_out6), .out7(decoder_1_out7), .sel(T[2:0]));  // open: en
  Decoder #(.select(3)) decoder_2 (
    .out0(decoder_2_out0), .out1(decoder_2_out1), .out2(decoder_2_out2), .out3(decoder_2_out3),
    .out4(decoder_2_out4), .out5(decoder_2_out5), .out6(decoder_2_out6), .out7(decoder_2_out7),
    .sel(IR[14:12]));  // open: en
  and and_1 (and_1_out, decoder_1_out4, decoder_2_out5);
  and and_2 (and_2_out, R, decoder_1_out1);
  and and_3 (and_3_out, decoder_1_out6, decoder_2_out6);
  and and_4 (and_4_out, decoder_1_out4, decoder_2_out3);
  or or_1 (or_1_out, and_1_out, and_2_out, and_3_out, and_4_out);
  not not_1 (Load, or_1_out);
endmodule

module adder_1 (
  input  x,
  input  y,
  input  c_in,
  output \output ,
  output cout
);

  wire and_1_out, and_2_out, xor_1_out;

  xor xor_1 (xor_1_out, x, y);
  and and_1 (and_1_out, c_in, xor_1_out);
  and and_2 (and_2_out, x, y);
  xor xor_2 (\output , xor_1_out, c_in);
  or or_1 (cout, and_1_out, and_2_out);
endmodule

module adder_12 (
  input  cin,
  input  [11:0] X,
  input  [11:0] Y,
  output [11:0] coutput,
  output cout
);

  wire adder_1_1_cout, adder_1_2_cout, adder_1_3_cout, adder_1_4_cout, adder_1_5_cout, adder_1_6_cout,
       adder_1_7_cout, adder_1_8_cout, adder_1_9_cout, adder_1_10_cout, adder_1_11_cout;

  adder_1 adder_1_1 (.x(X[0]), .y(Y[0]), .c_in(cin), .\output (coutput[0]), .cout(adder_1_1_cout));
  adder_1 adder_1_2 (.x(X[1]), .y(Y[1]), .c_in(adder_1_1_cout), .\output (coutput[1]), .cout(adder_1_2_cout));
  adder_1 adder_1_3 (.x(X[2]), .y(Y[2]), .c_in(adder_1_2_cout), .\output (coutput[2]), .cout(adder_1_3_cout));
  adder_1 adder_1_4 (.x(X[3]), .y(Y[3]), .c_in(adder_1_3_cout), .\output (coutput[3]), .cout(adder_1_4_cout));
  adder_1 adder_1_5 (.x(X[4]), .y(Y[4]), .c_in(adder_1_4_cout), .\output (coutput[4]), .cout(adder_1_5_cout));
  adder_1 adder_1_6 (.x(X[5]), .y(Y[5]), .c_in(adder_1_5_cout), .\output (coutput[5]), .cout(adder_1_6_cout));
  adder_1 adder_1_7 (.x(X[6]), .y(Y[6]), .c_in(adder_1_6_cout), .\output (coutput[6]), .cout(adder_1_7_cout));
  adder_1 adder_1_8 (.x(X[7]), .y(Y[7]), .c_in(adder_1_7_cout), .\output (coutput[7]), .cout(adder_1_8_cout));
  adder_1 adder_1_9 (.x(X[8]), .y(Y[8]), .c_in(adder_1_8_cout), .\output (coutput[8]), .cout(adder_1_9_cout));
  adder_1 adder_1_10 (.x(X[9]), .y(Y[9]), .c_in(adder_1_9_cout), .\output (coutput[9]), .cout(adder_1_10_cout));
  adder_1 adder_1_11 (.x(X[10]), .y(Y[10]), .c_in(adder_1_10_cout), .\output (coutput[10]), .cout(adder_1_11_cout));
  adder_1 adder_1_12 (.x(X[11]), .y(Y[11]), .c_in(adder_1_11_cout), .\output (coutput[11]), .cout(cout));
endmodule

module adder_16 (
  input  cin,
  input  [15:0] X,
  input  [15:0] Y,
  output [15:0] \output ,
  output cout
);

  wire adder_1_1_cout, adder_1_2_cout, adder_1_3_cout, adder_12_1_cout;

  adder_12 adder_12_1 (.X(X[11:0]), .Y(Y[11:0]), .coutput(\output [11:0]), .cout(adder_12_1_cout), .cin(cin));
  adder_1 adder_1_1 (.x(X[12]), .y(Y[12]), .c_in(adder_12_1_cout), .\output (\output [12]), .cout(adder_1_1_cout));
  adder_1 adder_1_2 (.x(X[13]), .y(Y[13]), .c_in(adder_1_1_cout), .\output (\output [13]), .cout(adder_1_2_cout));
  adder_1 adder_1_3 (.x(X[14]), .y(Y[14]), .c_in(adder_1_2_cout), .\output (\output [14]), .cout(adder_1_3_cout));
  adder_1 adder_1_4 (.x(X[15]), .y(Y[15]), .c_in(adder_1_3_cout), .\output (\output [15]), .cout(cout));
endmodule

module adder_3 (
  input  cin,
  input  [2:0] X,
  input  [2:0] Y,
  output [2:0] out_4,
  output out_5
);

  wire adder_1_1_cout, adder_1_2_cout;

  adder_1 adder_1_1 (.x(X[0]), .y(Y[0]), .c_in(cin), .\output (out_4[0]), .cout(adder_1_1_cout));
  adder_1 adder_1_2 (.x(X[1]), .y(Y[1]), .c_in(adder_1_1_cout), .\output (out_4[1]), .cout(adder_1_2_cout));
  adder_1 adder_1_3 (.x(X[2]), .y(Y[2]), .c_in(adder_1_2_cout), .\output (out_4[2]), .cout(out_5));
endmodule

module R (
  input  [2:0] T_count,
  input  E_IN,
  input  FGI,
  input  FGO,
  output E_OUT
);

  wire and_1_out, and_2_out, and_3_out, decoder_1_out0, decoder_1_out1, decoder_1_out2, or_1_out;

  or or_1 (or_1_out, FGI, FGO);
  Decoder #(.select(3)) decoder_1 (
    .out0(decoder_1_out0), .out1(decoder_1_out1), .out2(decoder_1_out2), .sel(T_count));  // open: out3, out4, out5, out6, out7, en
  and and_1 (and_1_out, ~decoder_1_out0, ~decoder_1_out1, ~decoder_1_out2);  // AND_Gate
  and and_2 (and_2_out, and_1_out, E_IN, or_1_out);
  and and_3 (and_3_out, decoder_1_out2, E_OUT);
  J_K_Flip_Flop j_k_ff_1 (.J(and_2_out), .clk(T_count[0]), .K(and_3_out), .Q(E_OUT));  // open: Qn, preset, en, reset
endmodule

module I_EN (
  input  EIN_J,
  input  Clock,
  input  EIN_K,
  output EIN_OUT
);

  J_K_Flip_Flop j_k_ff_1 (.J(EIN_J), .clk(Clock), .K(EIN_K), .Q(EIN_OUT));  // open: Qn, preset, en, reset
endmodule
